# Fritzing sketch RC car circuit diagram (saved by Fritzing 0.8.7b)
breadboards: 1

parts:
  S1 = H-Bridge with L298N
  M3 = DC Motor
  M4 = DC Motor
  Part1 = Arduino Nano (Rev3.0) (ICSP)
  VCC1 = 4 x AAA Battery Mount
  S3 = H-Bridge with L298N
  M5 = DC Motor
  M6 = DC Motor
  VCC2 = 4 x AAA Battery Mount  # not connected
  VCC3 = 4 x AAA Battery Mount  # not connected
  U1 = DC-DC_CONVERTER [package=dc-dc_converter]  # not connected
  Raspberry_Pi1 = Raspberry Pi (Model B)  # not connected

nets:
  12V: S1.12V, VCC1.+, S3.12V
  GND: S1.GND, Part1.GND, Part1.RESET, S3.GND
  5V: S1.5V, Part1.5V, Part1.A7, S3.5V
  N1: S1.ENA, Part1.D11/MOSI
  N2: S1.IN1, Part1.D8
  N3: S1.IN2, Part1.D7
  N4: S1.IN3, Part1.D3
  N5: S1.IN4, Part1.D2
  N6: S1.ENB, Part1.D10
  N7: S1.M1-01, M4.pin_2
  N8: S1.M1-02, M4.pin_1
  N9: S1.M2-01, M3.pin_2
  N10: S1.M2-02, M3.pin_1
  N11: Part1.D4, S3.IN1
  N12: Part1.D5, S3.ENA
  N13: Part1.D6, S3.ENB
  N14: Part1.D9, S3.IN2
  N15: Part1.D12/MISO, S3.IN3
  N16: Part1.D13/SCK, S3.IN4
  N17: S3.M1-01, M6.pin_2
  N18: S3.M1-02, M6.pin_1
  N19: S3.M2-01, M5.pin_2
  N20: S3.M2-02, M5.pin_1

custom parts:
  H-Bridge with L298N: h-bridge
  Raspberry Pi (Model B): Raspberry Pi Single-board Computer, Model B
